# Fritzing sketch smart_exp (saved by Fritzing 0.9.3b)
breadboards: 1

parts:
  hc-sr1 = hc-sr04
  S1 = Pushbutton [package="[THT]"]
  S2 = Pushbutton [package="[THT]"]
  LED1 = LED - 5mm [color="Red (633nm)" package="5 mm [THT]"]
  LED2 = LED - 5mm [color="Green (560nm)" package="5 mm [THT]"]
  PIR1 = PIR sensor
  Componente1 = Arduino Uno (Rev3)
  R1 = Resistor [tolerance=±5% resistance=220 package="0402 [SMD]"]
  R2 = Resistor [tolerance=±5% resistance=220 package="0402 [SMD]"]
  R3 = Resistor [tolerance=±5% resistance=10k package="0402 [SMD]"]
  R4 = Resistor [tolerance=±5% resistance=10k package="0402 [SMD]"]
  DHT1 = DHT11 Humitidy and Temperature Sensor (3 pins)
  J1 = Basic Servo
  R5 = Rotary Potentiometer (Small) [maximum_resistance=100kΩ package=THT]

nets:
  VCC: hc-sr1.VCC, S1.Pin_3, S1.Pin_4, S2.Pin_3, S2.Pin_4, PIR1.VDD, Componente1.5V, DHT1.VDD, J1.vcc, R5.leg2
  N1: hc-sr1.Trig, Componente1.D7
  N2: hc-sr1.Echo, Componente1.D8
  N3: S1.Pin_1, S1.Pin_2, Componente1.D3_PWM, R4.Pin_0
  N4: S2.Pin_1, S2.Pin_2, Componente1.D5_PWM, R3.Pin_0
  GND: LED1.cathode, LED2.cathode, PIR1.GND, Componente1.GND, R3.Pin_1, R4.Pin_1, DHT1.GND, J1.gnd, R5.leg1
  N5: LED1.anode, R1.Pin_0
  N6: LED2.anode, R2.Pin_0
  N7: PIR1.SIG, Componente1.D2
  N8: Componente1.A0, R5.wiper
  N9: Componente1.D11_PWM/MOSI, J1.pulse
  N10: Componente1.D12/MISO, R2.Pin_1
  N11: Componente1.D13/SCK, R1.Pin_1
  N12: Componente1.D6_PWM, DHT1.DATA

custom parts:
  DHT11 Humitidy and Temperature Sensor (3 pins): DHT11 Humidity and Temperature Sensor (3 pins) from the design created by John De Cristofaro for Adafruit Industries.
