# Fritzing sketch smart_dam (saved by Fritzing 0.9.3b)
breadboards: 1

parts:
  U1 = ESP8266 NodeMCU LoLin module
  LED1 = LED - 3mm [color="Green (565nm)" package="3 mm [THT]"]
  LED2 = LED - 3mm [color="Green (565nm)" package="3 mm [THT]"]
  U2 = HC-SR04 [chip_label=IC package="SIP (Single Inline) [THT]"]
  Componente1 = Arduino Uno (Rev3)
  J1 = Basic Servo
  BT1 = Bluetooth HC-06u [package=THT]

nets:
  N1: U1.D0, LED1.anode
  N2: U1.D1, U2.Trig
  N3: U1.D2, U2.Echo
  GND: U1.GND, LED1.cathode, LED2.cathode, U2.GND, Componente1.GND, J1.gnd, BT1.GND
  N4: U1.D5, BT1.TXD
  N5: U1.D6, BT1.RXD
  N6: U1.D7, Componente1.D2
  N7: U1.D8, Componente1.D3_PWM
  VIN: U1.Vin, Componente1.VIN
  N8: LED2.anode, Componente1.D6_PWM
  VCC: U2.Vcc, Componente1.5V, J1.vcc, BT1.VCC
  N9: Componente1.D8, J1.pulse

custom parts:
  ESP8266 NodeMCU LoLin module: ESP8266 based NodeMCU
  HC-SR04: HC-SR04 ultrasound distance sensor
  Bluetooth HC-06u: Bluetooth HC-06 - face up, pins down 16.5mm x 37.5mm PCB
